# Fritzing sketch CanINO (saved by Fritzing 0.9.10b)
breadboards: 1

parts:
  Part1 = Arduino Uno (Rev3)
  U1 = POT [knob_status=50% power=0.5W package=pot_mammoth]
  Grove1 = Grove OLED 128x96
  J2 = Basic Servo
  J3 = Basic Servo
  ZS-042_RTC1 = ZS-042 RTC Module  # not connected
  Part2 = HX711 Weighing Sensor Module  # not connected

nets:
  GND: Part1.GND, U1.E, Grove1.GND, J2.gnd, J3.gnd
  VCC: Part1.5V, U1.S, Grove1.VCC, J2.vcc, J3.vcc
